# Fritzing sketch LCD with I2C Arduino Nano via MQTT (saved by Fritzing 0.9.2b)
breadboards: 1

parts:
  Part1 = ENC28J60 Breakout Board
  Part2 = Arduino Nano (Rev3.0)
  LED1 = smd LED [color="Red (633nm)" package="0805 [SMD]"]
  LCM1602_IIC2 = LCM1602 IIC [part_number="LCM1602 IIC" chip_label="LCM1602 IIC" package="DIP (Dual Inline) [THT]"]
  LCD2 = LCD screen

nets:
  VCC: Part1.VCC, Part2.5V, LCM1602_IIC2.VCC
  GND: Part1.GND, Part2.GND, LED1.cathode, LCM1602_IIC2.GND
  N1: Part1.CS, Part2.D10
  N2: Part1.SI, Part2.D11/MOSI
  N3: Part1.SCK, Part2.D13/SCK
  N4: Part1.SO, Part2.D12/MISO
  N5: Part1.INT, Part2.D2
  N6: Part2.D6, LED1.anode
  N7: Part2.A5, LCM1602_IIC2.SCL
  N8: Part2.A4, LCM1602_IIC2.SDA
  VSS: LCM1602_IIC2.VSS, LCD2.VSS
  VDD: LCM1602_IIC2.VDD, LCD2.VDD
  N9: LCM1602_IIC2.V0, LCD2.V0
  N10: LCM1602_IIC2.RS, LCD2.RS
  N11: LCM1602_IIC2.RW, LCD2.R/W
  N12: LCM1602_IIC2.E, LCD2.E
  N13: LCM1602_IIC2.D0, LCD2.DB0
  N14: LCM1602_IIC2.D1, LCD2.DB1
  N15: LCM1602_IIC2.D2, LCD2.DB2
  N16: LCM1602_IIC2.D3, LCD2.DB3
  N17: LCM1602_IIC2.D4, LCD2.DB4
  N18: LCM1602_IIC2.D5, LCD2.DB5
  N19: LCM1602_IIC2.D6, LCD2.DB6
  N20: LCM1602_IIC2.D7, LCD2.DB7
  N21: LCM1602_IIC2.A, LCD2.LED+
  N22: LCM1602_IIC2.K, LCD2.LED-

custom parts:
  ENC28J60 Breakout Board: This is a breakout board for the Microchip ENC28J60 stand-alone ethernet controller. The ENC28J60 has an SPI interface. It operates at 3.3 Volts.
  LCM1602 IIC: I2C-Module to use a 1602 or 2004 LCD on with the wire.h libory Serial LCD Modul
